// Logisim project cpu.circ as structural Verilog: 1 circuit, main circuit main
module main (
);

  wire adder_1_cout, demultiplexer_1_out0, demultiplexer_1_out1, demultiplexer_1_out2, demultiplexer_1_out3,
       demultiplexer_1_out4, demultiplexer_1_out6, demultiplexer_1_out7, demultiplexer_2_out0,
       demultiplexer_2_out1, demultiplexer_2_out2, demultiplexer_2_out3, demultiplexer_2_out4,
       demultiplexer_2_out6, demultiplexer_2_out7, undriven_2, undriven_3, undriven_4, undriven_5,
       undriven_6, undriven_7, undriven_8, undriven_9, undriven_11;
  wire [0:0] or_1_out;
  wire [7:0] A_q, adder_2_out, B_q, BP_q, C_q, H_q, L_q, Main_Bus, MAR_q, register_1_q, register_2_q, SP_q,
       xor_1_out;
  wire [7:1] controlled_buffer_12_out;
  wire [7:7] undriven_10;
  wire [10:0] adder_1_out, controlled_buffer_1_out, controlled_buffer_2_out, demultiplexer_3_out0,
       demultiplexer_3_out2, PC_q, ram_1_dout, undriven;
  wire [10:4] demultiplexer_3_out1;
  wire [10:7] demultiplexer_3_out3;
  wire [10:8] controlled_buffer_4_out;

  Register MAR (.clk(undriven_2), .Q(MAR_q), .clr(1'b0));  // open: D, en
  ROM #(.addrWidth(11), .dataWidth(16), .misaligned("true")) Main_ROM (.addr(undriven));  // open: data
  RAM #(.dataWidth(11), .\type ("nonvolatile")) ram_1 (
    .addr(MAR_q), .we(undriven_5), .oe(undriven_4), .clk(undriven_2), .din(controlled_buffer_2_out),
    .dout(ram_1_dout));
  assign controlled_buffer_1_out = undriven_3 ? demultiplexer_3_out0 : 11'bz;  // Controlled_Buffer controlled_buffer_1
  Register #(.width(11)) PC (.D(controlled_buffer_1_out), .en(undriven_3), .Q(PC_q), .clr(1'b0));  // open: clk
  assign controlled_buffer_2_out = undriven_5 ? {3'b000, Main_Bus} : 11'bz;  // Controlled_Buffer controlled_buffer_2
  Controlled_Buffer #(.width(11)) controlled_buffer_3 (.in(adder_1_out), .out(controlled_buffer_1_out));  // open: en
  Adder #(.width(11)) adder_1 (.a(PC_q), .b(11'h1), .out(adder_1_out), .cout(adder_1_cout));  // open: cin
  assign {controlled_buffer_4_out, Main_Bus} = undriven_4 ? ram_1_dout : 11'bz;  // Controlled_Buffer controlled_buffer_4
  Demultiplexer #(.select(3)) demultiplexer_1 (
    .out0(demultiplexer_1_out0), .out1(demultiplexer_1_out1), .out2(demultiplexer_1_out2),
    .out3(demultiplexer_1_out3), .out4(demultiplexer_1_out4), .out6(demultiplexer_1_out6),
    .out7(demultiplexer_1_out7));  // open: out5, in, sel
  Demultiplexer #(.select(3)) demultiplexer_2 (
    .out0(demultiplexer_2_out0), .out1(demultiplexer_2_out1), .out2(demultiplexer_2_out2),
    .out3(demultiplexer_2_out3), .out4(demultiplexer_2_out4), .out6(demultiplexer_2_out6),
    .out7(demultiplexer_2_out7));  // open: out5, in, sel
  // NOT_Gate not_1 has open pins: in=undriven_2, out=open
  Register register_1 (.D(Main_Bus), .en(undriven_7), .clk(undriven_2), .Q(register_1_q), .clr(1'b0));
  Register register_2 (.D(Main_Bus), .en(undriven_6), .clk(undriven_2), .Q(register_2_q), .clr(1'b0));
  Register A (.D(Main_Bus), .en(demultiplexer_1_out0), .clk(undriven_2), .Q(A_q), .clr(1'b0));
  Register B (.D(Main_Bus), .en(demultiplexer_1_out1), .clk(undriven_2), .Q(B_q), .clr(1'b0));
  Register C (.D(Main_Bus), .en(demultiplexer_1_out2), .clk(undriven_2), .Q(C_q), .clr(1'b0));
  Register H (.D(Main_Bus), .en(demultiplexer_1_out3), .clk(undriven_2), .Q(H_q), .clr(1'b0));
  Register L (.D(Main_Bus), .en(demultiplexer_1_out4), .clk(undriven_2), .Q(L_q), .clr(1'b0));
  Register SP (.D(Main_Bus), .en(demultiplexer_1_out6), .clk(undriven_2), .Q(SP_q), .clr(1'b0));
  Register BP (.D(Main_Bus), .en(demultiplexer_1_out7), .clk(undriven_2), .Q(BP_q), .clr(1'b0));
  ROM #(.dataWidth(13)) rom_1 ();  // open: addr, data
  assign xor_1_out = register_2_q ^ {8{undriven_10[7]}};  // XOR_Gate xor_1, 8 bits wide
  assign Main_Bus = demultiplexer_2_out0 ? A_q : 8'bz;  // Controlled_Buffer controlled_buffer_5
  assign Main_Bus = demultiplexer_2_out1 ? B_q : 8'bz;  // Controlled_Buffer controlled_buffer_6
  assign Main_Bus = demultiplexer_2_out2 ? C_q : 8'bz;  // Controlled_Buffer controlled_buffer_7
  assign Main_Bus = demultiplexer_2_out3 ? H_q : 8'bz;  // Controlled_Buffer controlled_buffer_8
  assign Main_Bus = demultiplexer_2_out4 ? L_q : 8'bz;  // Controlled_Buffer controlled_buffer_9
  assign Main_Bus = demultiplexer_2_out6 ? SP_q : 8'bz;  // Controlled_Buffer controlled_buffer_10
  assign Main_Bus = demultiplexer_2_out7 ? BP_q : 8'bz;  // Controlled_Buffer controlled_buffer_11
  Adder adder_2 (.a(register_1_q), .b(xor_1_out), .out(adder_2_out));  // open: cin, cout
  assign {controlled_buffer_12_out, controlled_buffer_12_out[1]} = undriven_8 ? adder_2_out : 8'bz;  // Controlled_Buffer controlled_buffer_12
  Demultiplexer #(.select(2), .width(11)) demultiplexer_3 (
    .out0(demultiplexer_3_out0), .out1({demultiplexer_3_out1, {4{demultiplexer_3_out1[4]}}}),
    .out2(demultiplexer_3_out2), .out3({demultiplexer_3_out3, {7{demultiplexer_3_out3[7]}}}));  // open: in, sel
  or or_1 (or_1_out[0], controlled_buffer_12_out[1], controlled_buffer_12_out[1], controlled_buffer_12_out[2], controlled_buffer_12_out[3], controlled_buffer_12_out[4], controlled_buffer_12_out[5], controlled_buffer_12_out[6], controlled_buffer_12_out[7]);
  Register #(.width(2)) FLAGS (.D({controlled_buffer_12_out[7], or_1_out[0]}), .en(undriven_9));  // open: clk, Q, clr
  assign Main_Bus = undriven_11 ? demultiplexer_3_out2[7:0] : 8'bz;  // Controlled_Buffer controlled_buffer_13
  // also tied to GND on the sheet: {adder_1_cout, demultiplexer_3_out1[4], demultiplexer_3_out3[7]}

  // Notes on the sheet:
  //   contents of Main_ROM (hex, n*v repeats v):
  //   101 15*0 1010 15*0 111 31*0 1 15*0 10 15*0 10 15*0 10 8*0 d 22*0 100 15*0 10 15*0 1
endmodule
