// Logisim project new_cpu.circ as structural Verilog: 3 circuits, main circuit main
module main (
  input  FLAGS_MANUAL_ENABLE,
  input  IN_FLAG_LOAD_IR,
  input  IN_FLAG_INC_PC,
  input  IN_FLAG_REG_OE1,
  input  IN_FLAG_REG_IE1,
  input  IN_FLAG_ADDR_IN_PC,
  input  IN_FLAG_IMM_TO_BUS,
  input  IN_FLAG_REG_OE0,
  input  IN_FLAG_REG_IE0,
  input  IN_FLAG_RAM_MAR_WRITE,
  input  IN_FLAG_RAM_WRITE,
  input  IN_FLAG_RAM_READ,
  input  IN_FLAG_INC_MAR,
  input  IN_FLAG_DEC_MAR,
  input  IN_FLAG_ALU_IN0,
  input  IN_FLAG_ALU_IN1,
  input  IN_FLAG_ALU_OE,
  input  IN_FLAG_ASLU_SE,
  input  IN_FLAG_ALU_SET_C,
  input  IN_FLAG_ALU_CLR_C,
  input  IN_FLAG_NEXT_INS,
  input  IN_FLAG_UPDATE_FLAGS,
  input  IN_FLAG_HALT,
  input  CLOCK,
  output FLAG_LOAD_IR,
  output FLAG_INC_PC,
  output FLAG_REG_OE1,
  output FLAG_REG_IE1,
  output FLAG_ADDR_IN_PC,
  output FLAG_IMM_TO_BUS,
  output FLAG_REG_OE0,
  output FLAG_REG_IE0,
  output FLAG_RAM_MAR_WRITE,
  output FLAG_RAM_WRITE,
  output FLAG_RAM_READ,
  output FLAG_INC_MAR,
  output FLAG_DEC_MAR,
  output FLAG_ALU_IN0,
  output FLAG_ALU_IN1,
  output FLAG_ALU_OE,
  output FLAG_ALU_SE,
  output FLAG_ALU_SET_C,
  output FLAG_ALU_CLR_C,
  output FLAG_NEXT_INS,
  output FLAG_UPDATE_FLAGS,
  output FLAG_HALT
);

  wire and_1_out, and_2_out, demultiplexer_1_out0, demultiplexer_1_out1, demultiplexer_1_out2,
       demultiplexer_1_out3, demultiplexer_1_out4, demultiplexer_1_out5, demultiplexer_1_out6,
       demultiplexer_1_out7, demultiplexer_2_out0, demultiplexer_2_out1, demultiplexer_2_out2,
       demultiplexer_2_out3, demultiplexer_2_out4, demultiplexer_2_out5, demultiplexer_2_out6,
       demultiplexer_2_out7, not_1_out, not_2_out, not_3_out, not_4_out, not_5_out, or_1_out, or_2_out,
       or_3_out, or_4_out, or_5_out, s_r_ff_1_q, undriven_3;
  wire [1:0] and_3_out, bit_extender_1_out, REGISTER_INACCESSIBLE_FLAGS_q, undriven_4;
  wire [1:1] adder_2_cout;
  wire [2:0] adder_3_out, controlled_buffer_44_out, IP_OR_SO_q, undriven, undriven_2;
  wire [7:0] adder_1_out, BREGISTER_BP_q, controlled_buffer_1_out, controlled_buffer_14_out,
       controlled_buffer_15_out, controlled_buffer_16_out, controlled_buffer_17_out,
       controlled_buffer_18_out, controlled_buffer_19_out, controlled_buffer_20_out,
       controlled_buffer_21_out, controlled_buffer_22_out, register_1_q, register_2_q, REGISTER_A_q,
       REGISTER_B_q, REGISTER_C_q, REGISTER_H_q, REGISTER_INACCESSIBLE_MAR_q, REGISTER_L_q,
       s_11bit_to_8bit_1_s_out, s_11bit_to_8bit_2_s_out, s_11bit_to_8bit_3_s_out, s_11bit_to_8bit_4_s_out,
       s_11bit_to_8bit_5_s_out, s_11bit_to_8bit_6_s_out, s_11bit_to_8bit_7_s_out, s_11bit_to_8bit_8_s_out,
       s_11bit_to_8bit_9_s_out, s_11bit_to_8bit_10_s_out, SREGISTER_SP_q, xor_1_out, xor_2_out;
  wire [7:6] adder_2_out;
  wire [10:0] adder_4_out, controlled_buffer_4_out, controlled_buffer_47_out, demultiplexer_3_out1,
       demultiplexer_3_out3, MAIN_BUS, ram_1_dout, register_3_q, s_8bit_to_11bit_1_s_out,
       s_8bit_to_11bit_2_s_out, s_8bit_to_11bit_3_s_out, s_8bit_to_11bit_4_s_out, s_8bit_to_11bit_5_s_out,
       s_8bit_to_11bit_6_s_out, s_8bit_to_11bit_7_s_out, s_8bit_to_11bit_8_s_out, s_8bit_to_11bit_9_s_out;
  wire [10:4] demultiplexer_3_out2;
  wire [10:7] demultiplexer_3_out0;
  wire [15:0] controlled_buffer_43_out, Main_Rom_data, REGISTER_INACCESSIBLE_IR_q;

  assign controlled_buffer_1_out = FLAG_RAM_MAR_WRITE ? s_11bit_to_8bit_1_s_out : 8'bz;  // Controlled_Buffer controlled_buffer_1
  assign controlled_buffer_1_out = or_2_out ? adder_1_out : 8'bz;  // Controlled_Buffer controlled_buffer_2
  or or_1 (or_1_out, or_2_out, FLAG_RAM_MAR_WRITE);
  assign xor_1_out = 8'h1 ^ {8{FLAG_DEC_MAR}};  // XOR_Gate xor_1, 8 bits wide
  Register REGISTER_INACCESSIBLE_MAR (
    .D(controlled_buffer_1_out), .en(or_1_out), .clk(and_1_out), .Q(REGISTER_INACCESSIBLE_MAR_q), .clr(1'b0));
  or or_2 (or_2_out, FLAG_INC_MAR, FLAG_DEC_MAR);
  Adder adder_1 (.a(xor_1_out), .b(REGISTER_INACCESSIBLE_MAR_q), .out(adder_1_out), .cin(FLAG_DEC_MAR));  // open: cout
  RAM #(.dataWidth(11)) ram_1 (
    .addr(REGISTER_INACCESSIBLE_MAR_q), .we(FLAG_RAM_WRITE), .oe(FLAG_RAM_READ), .clk(and_1_out),
    .din(controlled_buffer_4_out), .dout(ram_1_dout));
  S_11BIT_TO_8BIT s_11bit_to_8bit_1 (.S_IN(MAIN_BUS), .S_OUT(s_11bit_to_8bit_1_s_out));
  assign MAIN_BUS = FLAG_RAM_READ ? ram_1_dout : 11'bz;  // Controlled_Buffer controlled_buffer_3
  assign controlled_buffer_4_out = FLAG_RAM_WRITE ? MAIN_BUS : 11'bz;  // Controlled_Buffer controlled_buffer_4
  assign MAIN_BUS = demultiplexer_2_out0 ? s_8bit_to_11bit_1_s_out : 11'bz;  // Controlled_Buffer controlled_buffer_5
  S_8BIT_TO_11BIT s_8bit_to_11bit_1 (.S_IN(REGISTER_A_q), .S_OUT(s_8bit_to_11bit_1_s_out));
  assign MAIN_BUS = demultiplexer_2_out1 ? s_8bit_to_11bit_2_s_out : 11'bz;  // Controlled_Buffer controlled_buffer_6
  S_8BIT_TO_11BIT s_8bit_to_11bit_2 (.S_IN(REGISTER_B_q), .S_OUT(s_8bit_to_11bit_2_s_out));
  assign MAIN_BUS = demultiplexer_2_out2 ? s_8bit_to_11bit_3_s_out : 11'bz;  // Controlled_Buffer controlled_buffer_7
  S_8BIT_TO_11BIT s_8bit_to_11bit_3 (.S_IN(REGISTER_C_q), .S_OUT(s_8bit_to_11bit_3_s_out));
  assign MAIN_BUS = demultiplexer_2_out3 ? s_8bit_to_11bit_4_s_out : 11'bz;  // Controlled_Buffer controlled_buffer_8
  S_8BIT_TO_11BIT s_8bit_to_11bit_4 (.S_IN(REGISTER_H_q), .S_OUT(s_8bit_to_11bit_4_s_out));
  assign MAIN_BUS = demultiplexer_2_out4 ? s_8bit_to_11bit_5_s_out : 11'bz;  // Controlled_Buffer controlled_buffer_9
  S_8BIT_TO_11BIT s_8bit_to_11bit_5 (.S_IN(REGISTER_L_q), .S_OUT(s_8bit_to_11bit_5_s_out));
  assign MAIN_BUS = demultiplexer_2_out6 ? s_8bit_to_11bit_6_s_out : 11'bz;  // Controlled_Buffer controlled_buffer_10
  S_8BIT_TO_11BIT s_8bit_to_11bit_6 (.S_IN(SREGISTER_SP_q), .S_OUT(s_8bit_to_11bit_6_s_out));
  assign MAIN_BUS = demultiplexer_2_out7 ? s_8bit_to_11bit_7_s_out : 11'bz;  // Controlled_Buffer controlled_buffer_11
  S_8BIT_TO_11BIT s_8bit_to_11bit_7 (.S_IN(BREGISTER_BP_q), .S_OUT(s_8bit_to_11bit_7_s_out));
  assign MAIN_BUS = FLAG_ALU_OE ? s_8bit_to_11bit_8_s_out : 11'bz;  // Controlled_Buffer controlled_buffer_12
  S_8BIT_TO_11BIT s_8bit_to_11bit_8 (.S_IN({adder_2_out, {6{adder_2_out[6]}}}), .S_OUT(s_8bit_to_11bit_8_s_out));
  assign MAIN_BUS = FLAG_IMM_TO_BUS ? s_8bit_to_11bit_9_s_out : 11'bz;  // Controlled_Buffer controlled_buffer_13
  S_8BIT_TO_11BIT s_8bit_to_11bit_9 (.S_IN(demultiplexer_3_out1[7:0]), .S_OUT(s_8bit_to_11bit_9_s_out));
  not not_1 (not_1_out, FLAG_ALU_CLR_C);
  and and_1 (and_1_out, CLOCK, not_1_out);
  S_11BIT_TO_8BIT s_11bit_to_8bit_2 (.S_IN(MAIN_BUS), .S_OUT(s_11bit_to_8bit_2_s_out));
  S_11BIT_TO_8BIT s_11bit_to_8bit_3 (.S_IN(MAIN_BUS), .S_OUT(s_11bit_to_8bit_3_s_out));
  S_11BIT_TO_8BIT s_11bit_to_8bit_4 (.S_IN(MAIN_BUS), .S_OUT(s_11bit_to_8bit_4_s_out));
  S_11BIT_TO_8BIT s_11bit_to_8bit_5 (.S_IN(MAIN_BUS), .S_OUT(s_11bit_to_8bit_5_s_out));
  S_11BIT_TO_8BIT s_11bit_to_8bit_6 (.S_IN(MAIN_BUS), .S_OUT(s_11bit_to_8bit_6_s_out));
  S_11BIT_TO_8BIT s_11bit_to_8bit_7 (.S_IN(MAIN_BUS), .S_OUT(s_11bit_to_8bit_7_s_out));
  S_11BIT_TO_8BIT s_11bit_to_8bit_8 (.S_IN(MAIN_BUS), .S_OUT(s_11bit_to_8bit_8_s_out));
  S_11BIT_TO_8BIT s_11bit_to_8bit_9 (.S_IN(MAIN_BUS), .S_OUT(s_11bit_to_8bit_9_s_out));
  S_11BIT_TO_8BIT s_11bit_to_8bit_10 (.S_IN(MAIN_BUS), .S_OUT(s_11bit_to_8bit_10_s_out));
  Demultiplexer #(.select(3)) demultiplexer_1 (
    .out0(demultiplexer_1_out0), .out1(demultiplexer_1_out1), .out2(demultiplexer_1_out2),
    .out3(demultiplexer_1_out3), .out4(demultiplexer_1_out4), .out5(demultiplexer_1_out5),
    .out6(demultiplexer_1_out6), .out7(demultiplexer_1_out7), .in(FLAG_REG_IE0), .sel(undriven_2));
  Register register_1 (.D(controlled_buffer_14_out), .en(FLAG_ALU_IN1), .clk(and_1_out), .Q(register_1_q), .clr(1'b0));
  assign controlled_buffer_14_out = FLAG_ALU_IN1 ? s_11bit_to_8bit_9_s_out : 8'bz;  // Controlled_Buffer controlled_buffer_14
  Register register_2 (.D(controlled_buffer_15_out), .en(FLAG_ALU_IN0), .clk(and_1_out), .Q(register_2_q), .clr(1'b0));
  assign controlled_buffer_15_out = FLAG_ALU_IN0 ? s_11bit_to_8bit_10_s_out : 8'bz;  // Controlled_Buffer controlled_buffer_15
  Register REGISTER_A (
    .D(controlled_buffer_16_out), .en(demultiplexer_1_out0), .clk(and_1_out), .Q(REGISTER_A_q), .clr(1'b0));
  assign controlled_buffer_16_out = demultiplexer_1_out0 ? s_11bit_to_8bit_2_s_out : 8'bz;  // Controlled_Buffer controlled_buffer_16
  Register REGISTER_B (
    .D(controlled_buffer_17_out), .en(demultiplexer_1_out1), .clk(and_1_out), .Q(REGISTER_B_q), .clr(1'b0));
  assign controlled_buffer_17_out = demultiplexer_1_out1 ? s_11bit_to_8bit_3_s_out : 8'bz;  // Controlled_Buffer controlled_buffer_17
  Register REGISTER_C (
    .D(controlled_buffer_18_out), .en(demultiplexer_1_out2), .clk(and_1_out), .Q(REGISTER_C_q), .clr(1'b0));
  assign controlled_buffer_18_out = demultiplexer_1_out2 ? s_11bit_to_8bit_4_s_out : 8'bz;  // Controlled_Buffer controlled_buffer_18
  Register REGISTER_H (
    .D(controlled_buffer_19_out), .en(demultiplexer_1_out3), .clk(and_1_out), .Q(REGISTER_H_q), .clr(1'b0));
  assign controlled_buffer_19_out = demultiplexer_1_out3 ? s_11bit_to_8bit_5_s_out : 8'bz;  // Controlled_Buffer controlled_buffer_19
  Register REGISTER_L (
    .D(controlled_buffer_20_out), .en(demultiplexer_1_out4), .clk(and_1_out), .Q(REGISTER_L_q), .clr(1'b0));
  assign controlled_buffer_20_out = demultiplexer_1_out4 ? s_11bit_to_8bit_6_s_out : 8'bz;  // Controlled_Buffer controlled_buffer_20
  Register SREGISTER_SP (
    .D(controlled_buffer_21_out), .en(demultiplexer_1_out6), .clk(and_1_out), .Q(SREGISTER_SP_q), .clr(1'b0));
  assign controlled_buffer_21_out = demultiplexer_1_out6 ? s_11bit_to_8bit_7_s_out : 8'bz;  // Controlled_Buffer controlled_buffer_21
  Register BREGISTER_BP (
    .D(controlled_buffer_22_out), .en(demultiplexer_1_out7), .clk(and_1_out), .Q(BREGISTER_BP_q), .clr(1'b0));
  assign controlled_buffer_22_out = demultiplexer_1_out7 ? s_11bit_to_8bit_8_s_out : 8'bz;  // Controlled_Buffer controlled_buffer_22
  assign xor_2_out = register_2_q ^ {8{FLAG_ALU_SE}};  // XOR_Gate xor_2, 8 bits wide
  Demultiplexer #(.select(3)) demultiplexer_2 (
    .out0(demultiplexer_2_out0), .out1(demultiplexer_2_out1), .out2(demultiplexer_2_out2),
    .out3(demultiplexer_2_out3), .out4(demultiplexer_2_out4), .out5(demultiplexer_2_out5),
    .out6(demultiplexer_2_out6), .out7(demultiplexer_2_out7), .in(FLAG_REG_OE0), .sel(undriven));
  S_R_Flip_Flop s_r_ff_1 (
    .S(FLAG_ALU_SET_C), .R(FLAG_ALU_CLR_C), .clk(and_1_out), .Q(s_r_ff_1_q));  // open: reset, Qn, preset
  or or_3 (or_3_out, FLAG_ALU_SE, s_r_ff_1_q);
  Adder adder_2 (
    .a(register_1_q), .b(xor_2_out), .out({adder_2_out, {6{adder_2_out[6]}}}), .cin(or_3_out),
    .cout(adder_2_cout[1]));
  assign FLAG_LOAD_IR = FLAGS_MANUAL_ENABLE ? IN_FLAG_LOAD_IR : 1'bz;  // Controlled_Buffer controlled_buffer_23
  assign FLAG_INC_PC = FLAGS_MANUAL_ENABLE ? IN_FLAG_INC_PC : 1'bz;  // Controlled_Buffer controlled_buffer_24
  assign FLAG_ADDR_IN_PC = FLAGS_MANUAL_ENABLE ? IN_FLAG_ADDR_IN_PC : 1'bz;  // Controlled_Buffer controlled_buffer_25
  assign FLAG_IMM_TO_BUS = FLAGS_MANUAL_ENABLE ? IN_FLAG_IMM_TO_BUS : 1'bz;  // Controlled_Buffer controlled_buffer_26
  assign FLAG_REG_OE0 = FLAGS_MANUAL_ENABLE ? IN_FLAG_REG_OE0 : 1'bz;  // Controlled_Buffer controlled_buffer_27
  assign FLAG_REG_IE0 = FLAGS_MANUAL_ENABLE ? IN_FLAG_REG_IE0 : 1'bz;  // Controlled_Buffer controlled_buffer_28
  assign FLAG_RAM_MAR_WRITE = FLAGS_MANUAL_ENABLE ? IN_FLAG_RAM_MAR_WRITE : 1'bz;  // Controlled_Buffer controlled_buffer_29
  assign FLAG_RAM_WRITE = FLAGS_MANUAL_ENABLE ? IN_FLAG_RAM_WRITE : 1'bz;  // Controlled_Buffer controlled_buffer_30
  assign FLAG_RAM_READ = FLAGS_MANUAL_ENABLE ? IN_FLAG_RAM_READ : 1'bz;  // Controlled_Buffer controlled_buffer_31
  assign FLAG_INC_MAR = FLAGS_MANUAL_ENABLE ? IN_FLAG_INC_MAR : 1'bz;  // Controlled_Buffer controlled_buffer_32
  assign FLAG_DEC_MAR = FLAGS_MANUAL_ENABLE ? IN_FLAG_DEC_MAR : 1'bz;  // Controlled_Buffer controlled_buffer_33
  assign FLAG_ALU_IN0 = FLAGS_MANUAL_ENABLE ? IN_FLAG_ALU_IN0 : 1'bz;  // Controlled_Buffer controlled_buffer_34
  assign FLAG_ALU_IN1 = FLAGS_MANUAL_ENABLE ? IN_FLAG_ALU_IN1 : 1'bz;  // Controlled_Buffer controlled_buffer_35
  assign FLAG_ALU_OE = FLAGS_MANUAL_ENABLE ? IN_FLAG_ALU_OE : 1'bz;  // Controlled_Buffer controlled_buffer_36
  assign FLAG_ALU_SE = FLAGS_MANUAL_ENABLE ? IN_FLAG_ASLU_SE : 1'bz;  // Controlled_Buffer controlled_buffer_37
  assign FLAG_ALU_SET_C = FLAGS_MANUAL_ENABLE ? IN_FLAG_ALU_SET_C : 1'bz;  // Controlled_Buffer controlled_buffer_38
  assign FLAG_ALU_CLR_C = FLAGS_MANUAL_ENABLE ? IN_FLAG_ALU_CLR_C : 1'bz;  // Controlled_Buffer controlled_buffer_39
  assign FLAG_NEXT_INS = FLAGS_MANUAL_ENABLE ? IN_FLAG_NEXT_INS : 1'bz;  // Controlled_Buffer controlled_buffer_40
  assign FLAG_UPDATE_FLAGS = FLAGS_MANUAL_ENABLE ? IN_FLAG_UPDATE_FLAGS : 1'bz;  // Controlled_Buffer controlled_buffer_41
  assign FLAG_HALT = FLAGS_MANUAL_ENABLE ? IN_FLAG_HALT : 1'bz;  // Controlled_Buffer controlled_buffer_42
  ROM #(.addrWidth(11), .dataWidth(16)) Main_Rom (.addr(register_3_q), .data(Main_Rom_data));
  Register #(.width(2)) REGISTER_INACCESSIBLE_FLAGS (
    .D({adder_2_cout[1], adder_2_out[7]}), .en(FLAG_UPDATE_FLAGS), .clk(and_1_out),
    .Q(REGISTER_INACCESSIBLE_FLAGS_q), .clr(1'b0));
  assign controlled_buffer_43_out = FLAG_LOAD_IR ? Main_Rom_data : 16'bz;  // Controlled_Buffer controlled_buffer_43
  and and_2 (and_2_out, not_2_out, not_3_out, REGISTER_INACCESSIBLE_IR_q[15]);
  Register #(.width(16)) REGISTER_INACCESSIBLE_IR (
    .D(controlled_buffer_43_out), .en(FLAG_LOAD_IR),
    .Q({REGISTER_INACCESSIBLE_IR_q[15:12], REGISTER_INACCESSIBLE_IR_q[12], REGISTER_INACCESSIBLE_IR_q[10:0]}),
    .clk(and_1_out), .clr(1'b0));
  not not_2 (not_2_out, REGISTER_INACCESSIBLE_IR_q[13]);
  not not_3 (not_3_out, REGISTER_INACCESSIBLE_IR_q[14]);
  not not_4 (not_4_out, FLAG_NEXT_INS);
  Demultiplexer #(.select(2), .width(11)) demultiplexer_3 (
    .out0({demultiplexer_3_out0, {7{demultiplexer_3_out0[7]}}}), .out1(demultiplexer_3_out1),
    .out2({demultiplexer_3_out2, {4{demultiplexer_3_out2[4]}}}), .out3(demultiplexer_3_out3),
    .in(REGISTER_INACCESSIBLE_IR_q[10:0]), .sel(undriven_4));
  assign controlled_buffer_44_out = FLAG_NEXT_INS ? 3'b000 : 3'bz;  // Controlled_Buffer controlled_buffer_44
  or or_4 (or_4_out, not_4_out, FLAG_NEXT_INS);
  assign MAIN_BUS = demultiplexer_2_out5 ? register_3_q : 11'bz;  // Controlled_Buffer controlled_buffer_45
  assign bit_extender_1_out = {{1{and_2_out}}, and_2_out};  // Bit_Extender bit_extender_1
  Adder #(.width(3)) adder_3 (.a(3'b001), .b(IP_OR_SO_q), .out(adder_3_out), .cin(1'b0));  // open: cout
  Register #(.width(3)) IP_OR_SO (
    .D(controlled_buffer_44_out), .en(or_4_out), .clk(not_5_out), .Q(IP_OR_SO_q), .clr(1'b0));
  assign controlled_buffer_44_out = not_4_out ? adder_3_out : 3'bz;  // Controlled_Buffer controlled_buffer_46
  not not_5 (not_5_out, and_1_out);
  assign controlled_buffer_47_out = demultiplexer_1_out5 ? MAIN_BUS : 11'bz;  // Controlled_Buffer controlled_buffer_47
  assign and_3_out = bit_extender_1_out & REGISTER_INACCESSIBLE_FLAGS_q;  // AND_Gate and_3, 2 bits wide
  assign controlled_buffer_47_out = FLAG_INC_PC ? adder_4_out : 11'bz;  // Controlled_Buffer controlled_buffer_48
  or or_5 (or_5_out, demultiplexer_1_out5, FLAG_INC_PC, undriven_3, FLAG_ADDR_IN_PC);
  ROM #(.dataWidth(32)) rom_1 (.addr({REGISTER_INACCESSIBLE_IR_q[15:12], REGISTER_INACCESSIBLE_IR_q[12], IP_OR_SO_q}));  // open: data
  Register #(.width(11)) register_3 (
    .D(controlled_buffer_47_out), .en(or_5_out), .clk(and_1_out), .Q(register_3_q), .clr(1'b0));
  assign controlled_buffer_47_out = FLAG_ADDR_IN_PC ? demultiplexer_3_out3 : 11'bz;  // Controlled_Buffer controlled_buffer_49
  Adder #(.width(11)) adder_4 (.a(register_3_q), .b(11'h1), .out(adder_4_out), .cin(1'b0));  // open: cout
  // also tied to GND on the sheet: {adder_2_out[6], demultiplexer_3_out0[7], demultiplexer_3_out2[4], REGISTER_INACCESSIBLE_IR_q[12]}
endmodule

module S_11BIT_TO_8BIT (
  input  [10:0] S_IN,
  output [7:0] S_OUT
);


  assign S_OUT = S_IN[7:0];
endmodule

module S_8BIT_TO_11BIT (
  input  [7:0] S_IN,
  output [10:0] S_OUT
);


  assign S_OUT = {3'b000, S_IN};
endmodule
